// Logisim project TP2.circ as structural Verilog
module Multiplexer (
  input  A,
  input  B,
  input  Selecteur,
  input  in_4,
  input  in_5,
  input  in_6,
  output S1,
  output out_8
);

  wire and_1_out, and_2_out, not_1_out;

  not not_1 (not_1_out, Selecteur);
  Multiplexer_part multiplexer_1 (.in0(in_4), .in1(in_5), .out(out_8), .sel(in_6));  // open: en
  and and_1 (and_1_out, B, not_1_out);
  and and_2 (and_2_out, A, Selecteur);
  or or_1 (S1, and_1_out, and_2_out);
endmodule

module Decodeur (
  input  A,
  input  B,
  input  C,
  input  [2:0] in_4,
  output S1,
  output S2,
  output S3,
  output S4,
  output S5,
  output S6,
  output S7,
  output S8,
  output [7:0] out_13
);

  wire not_1_out, not_2_out, not_3_out;

  not not_1 (not_1_out, A);
  not not_2 (not_2_out, B);
  not not_3 (not_3_out, C);
  Decoder #(.select(3)) decoder_1 (
    .out0(out_13[0]), .out1(out_13[1]), .out2(out_13[2]), .out3(out_13[3]), .out4(out_13[4]),
    .out5(out_13[5]), .out6(out_13[6]), .out7(out_13[7]), .sel(in_4));  // open: en
  and and_1 (S1, A, B, C);
  and and_2 (S2, not_1_out, B, C);
  and and_3 (S3, A, not_2_out, C);
  and and_4 (S4, A, B, not_3_out);
  and and_5 (S5, not_1_out, not_2_out, C);
  and and_6 (S6, A, not_2_out, not_3_out);
  and and_7 (S7, not_1_out, B, not_3_out);
  and and_8 (S8, not_1_out, not_2_out, not_3_out);
endmodule

module Additionneur_1_bit (
  input  A1,
  input  A2,
  input  R,
  output S1,
  output S2
);

  wire and_1_out, and_2_out, xor_1_out;

  xor xor_1 (xor_1_out, A1, A2);
  and and_1 (and_1_out, A1, A2);
  xor xor_2 (S1, xor_1_out, R);
  and and_2 (and_2_out, xor_1_out, R);
  or or_1 (S2, and_1_out, and_2_out);
endmodule

module Additionneur_4_bits (
  input  in_1,
  input  in_2,
  input  in_3,
  input  in_4,
  input  in_5,
  input  in_6,
  input  in_7,
  input  in_8,
  input  in_9,
  output out_10,
  output out_11,
  output out_12,
  output out_13,
  output out_14
);

  wire additionneur_1_bit_1_s2, additionneur_1_bit_2_s2, additionneur_1_bit_3_s2;

  Additionneur_1_bit additionneur_1_bit_1 (.A1(in_2), .A2(in_3), .R(in_1), .S1(out_11), .S2(additionneur_1_bit_1_s2));
  Additionneur_1_bit additionneur_1_bit_2 (
    .A1(in_4), .A2(in_5), .R(additionneur_1_bit_1_s2), .S1(out_12), .S2(additionneur_1_bit_2_s2));
  Additionneur_1_bit additionneur_1_bit_3 (
    .A1(in_6), .A2(in_7), .R(additionneur_1_bit_2_s2), .S1(out_13), .S2(additionneur_1_bit_3_s2));
  Additionneur_1_bit additionneur_1_bit_4 (.A1(in_8), .A2(in_9), .R(additionneur_1_bit_3_s2), .S1(out_14), .S2(out_10));
endmodule
