// Logisim project tp5_cpt4.circ as structural Verilog: 2 circuits, main circuit cpt4
module cpt4 (
  output halt,
  output [3:0] out_2
);

  wire clock_1_out;
  wire [3:0] adder_1_out;

  and and_1 (halt, out_2[0], out_2[1], out_2[2], out_2[3]);
  Clock clock_1 (.out(clock_1_out));
  D_Flip_Flop d_ff_1 (.clk(clock_1_out), .D(adder_1_out[3]), .Q(out_2[3]));  // open: Qn, preset, en, reset
  D_Flip_Flop d_ff_2 (.clk(clock_1_out), .D(adder_1_out[2]), .Q(out_2[2]));  // open: Qn, preset, en, reset
  D_Flip_Flop d_ff_3 (.clk(clock_1_out), .D(adder_1_out[1]), .Q(out_2[1]));  // open: Qn, preset, en, reset
  D_Flip_Flop d_ff_4 (.clk(clock_1_out), .D(adder_1_out[0]), .Q(out_2[0]));  // open: Qn, preset, en, reset
  Adder #(.width(4)) adder_1 (.a(4'b0000), .b(out_2), .out(adder_1_out), .cin(1'b1));  // open: cout

  // Notes on the sheet:
  //   valeur courante
  //   Compteur 4 bits
endmodule

module main (
  output halt,
  output [3:0] out_2,
  output [3:0] out_3,
  output same
);

  wire clock_1_out;

  Clock clock_1 (.out(clock_1_out));
  Counter #(.width(4), .max('hf)) counter_1 (.Q(out_2), .carry(halt), .clk(clock_1_out));  // open: load, D, count, clr
  cpt4 cpt4_1 (.halt(out_3[0]));  // open: out_2
  Comparator #(.width(4), .mode("unsigned")) comparator_1 (.a(out_3), .b(out_2), .eq(same));  // open: gt, lt
  // Pins of 1 and 4 bits meet at out_3
endmodule
